# Fritzing sketch doorlock_v1 (saved by Fritzing 0.9.2b)
circuit board: 4.9cm x 2.8cm
breadboards: 1

parts:
  ESP07 = ESP8266 WiFi Module [part_number=ESP8266]
  RFID = RFID-RC522-v2
  Power = screw terminal, 3 pins
  Serial = female pin header, 5 pins [form="♀ (female)"]
  Reset = Pushbutton [package="[THT]"]
  Mosfet_Pulldown = Resistor [tolerance=±5% resistance=10k package=THT]
  Reset_Pullup = Resistor [tolerance=±5% resistance=10k package=THT]
  Enable_Pullup = Resistor [tolerance=±5% resistance=10k package=THT]
  Prog = Pushbutton [package="[THT]"]
  Run_Pullup = Resistor [tolerance=±5% resistance=10k package=THT]
  LED = female pin header, 3 pins [form="♀ (female)"]
  MOSFET = MOSFET-NCHANNEL [package=to220v]
  Gate_Limit = Resistor [tolerance=±10% resistance=220 package=THT]

nets:
  N1: ESP07.RXD, Serial.pin2
  VCC: ESP07.VCC, RFID.3.3V, Power.pin2, Serial.pin1, Reset_Pullup.Pin_1, Enable_Pullup.Pin_0, Run_Pullup.Pin_1, LED.pin2
  N2: ESP07.GPIO_0, Prog.Pin_3, Prog.Pin_4, Run_Pullup.Pin_0
  N3: ESP07.GPIO_2, LED.pin3
  N4: ESP07.CH_PD, Enable_Pullup.Pin_1
  GND: ESP07.GND, RFID.GND, Power.pin1, Serial.pin4, Reset.Pin_1, Reset.Pin_2, Mosfet_Pulldown.Pin_0, Prog.Pin_1, Prog.Pin_2, LED.pin1, MOSFET.S
  N5: ESP07.TXD, Serial.pin3
  N6: ESP07.GPIO_15, RFID.SDA
  N7: ESP07.GPIO_5, RFID.RST
  N8: ESP07.GPIO_16, Gate_Limit.Pin_0
  N9: ESP07.GPIO_14, RFID.SCK
  N10: ESP07.GPIO_12, RFID.MISO
  N11: ESP07.GPIO_13, RFID.MOSI
  N12: ESP07.REST, Reset.Pin_4, Reset_Pullup.Pin_0
  N13: Power.pin3, MOSFET.D
  N14: Mosfet_Pulldown.Pin_1, MOSFET.G, Gate_Limit.Pin_1

notes:
  Gnd  +3v  Out
  Gnd Vcc Din
  3v Tx Rx Gd 5v
  S         G

custom parts:
  RFID-RC522-v2: A simple China made RFID-RC522 Reader; do check the pin labels, as this is a MFRC522 based clone.
